# Fritzing sketch nRF24L01_wireless_interface (saved by Fritzing 0.9.2b)

parts:
  Part2 = Arduino Pro Mini v13
  U1 = POT [package=pot_alpha_rv16af-20]
  Part1 = NRF24L01
  Part3 = Arduino Pro Mini v13
  Part4 = NRF24L01

nets:
  GND: Part2.GND, Part1.GND
  VCC: Part2.VCC, Part1.VCC
  N1: Part2.A0, U1.S
  N2: Part2.D13/SCK, Part1.SCK
  N3: Part2.D12/MISO, Part1.MISO
  N4: Part2.D11_PWM/MOSI, Part1.MOSI
  N5: Part2.D8, Part1.CSN
  N6: Part2.D7, Part1.CE
  GND_2: Part3.GND, Part4.GND
  VCC_2: Part3.VCC, Part4.VCC
  N7: Part3.D13/SCK, Part4.SCK
  N8: Part3.D12/MISO, Part4.MISO
  N9: Part3.D11_PWM/MOSI, Part4.MOSI
  N10: Part3.D8, Part4.CSN
  N11: Part3.D7, Part4.CE

notes:
  RX Connections
  TX Connections
  Rx and Tx connections are exactly same except for potentiometer.
  Arduino--nRF >>> VCC--VCC, GND--GND, 7--CE, 8--CSN, 11--MOSI, 12--MISO, 13--SCK
  On Tx side, potentiometer's middle terminal connects to A0 pin of Arduino Pro Mini.
